// Logisim project ALU.circ as structural Verilog: 2 circuits, main circuit main
module main (
  input  [3:0] in_1,
  input  [15:0] in_2,
  input  [15:0] in_3,
  output out_4,
  output out_5,
  output [15:0] out_6
);

  wire [15:0] Arithmetic_out, Logic_out, shifting_out;

  LogicUnit logicunit_1 (.BUS_A(in_2), .BUS_B(in_3), .Logic_control(in_1[1:0]), .Logic_unit_result(Logic_out));
  ShiftingUnitCircuit shiftingunitcircuit_1 (.Operand(in_2), .SA(in_3[3:0]), .OP(in_1[1:0]), .Operand_2(shifting_out));
  alu_arithmetic alu_arithmetic_1 (
    .Overflow(out_4), .Output(Arithmetic_out), .in_2(in_3), .in_3(in_2), .Zero(out_5), .Operation(in_1[1:0]));
  Multiplexer #(.select(2), .width(16), .enable("false")) multiplexer_1 (
    .in0(Logic_out), .in1(Arithmetic_out), .in2(shifting_out), .in3(shifting_out), .out(out_6),
    .sel(in_1[3:2]));

  // Other names for the same wires on the sheet: A[15:0] = in_2; B[15:0] = in_3; MainALU_output[15:0] = out_6;
  //   Operation[3:0] = in_1; sectionselc[1:0] = in_1[1:0]; Main_selc[1:0] = in_1[3:2]; overflow = out_4; zero = out_5
endmodule

module ALU (
  input  [3:0] in_1,
  input  [15:0] in_2,
  input  [15:0] in_3,
  output out_4,
  output out_5,
  output [15:0] out_6
);

  wire [15:0] Arithmetic_out, Logic_out, shifting_out;

  LogicUnit logicunit_1 (.BUS_A(in_2), .BUS_B(in_3), .Logic_control(in_1[1:0]), .Logic_unit_result(Logic_out));
  ShiftingUnitCircuit shiftingunitcircuit_1 (.Operand(in_2), .SA(in_3[3:0]), .OP(in_1[1:0]), .Operand_2(shifting_out));
  alu_arithmetic alu_arithmetic_1 (
    .Overflow(out_4), .Output(Arithmetic_out), .in_2(in_3), .in_3(in_2), .Zero(out_5), .Operation(in_1[1:0]));
  Multiplexer #(.select(2), .width(16), .enable("false")) multiplexer_1 (
    .in0(Logic_out), .in1(Arithmetic_out), .in2(shifting_out), .in3(shifting_out), .out(out_6),
    .sel(in_1[3:2]));

  // Other names for the same wires on the sheet: A[15:0] = in_2; B[15:0] = in_3; MainALU_output[15:0] = out_6;
  //   Operation[3:0] = in_1; sectionselc[1:0] = in_1[1:0]; Main_selc[1:0] = in_1[3:2]; overflow = out_4; zero = out_5
endmodule
