// Logisim project ControlUnitC.circ as structural Verilog: 4 circuits, main circuit ControlUnit
module ControlUnit (
  input  [4:0] Opcode,
  input  [1:0] Function,
  output [3:0] ALUop,
  output ALUSrc,
  output signExtend,
  output RegWrite,
  output [1:0] RegDest,
  output [1:0] RegWSrc,
  output memoryRead,
  output memoryWrite,
  output [1:0] PCSrc,
  output [1:0] BrachOP,
  output JumpOP
);

  ALUControlUnit alucontrolunit_1 (
    .OP0(Opcode[0]), .OP1(Opcode[1]), .OP2(Opcode[2]), .OP3(Opcode[3]), .OP4(Opcode[4]), .F0(Function[0]),
    .F1(Function[1]), .ALUop0(ALUop[0]), .ALUop1(ALUop[1]), .ALUop2(ALUop[2]), .ALUop3(ALUop[3]),
    .ALUSrc(ALUSrc), .signExtend(signExtend));
  RegistersMemoryControlUnit registersmemorycontrolunit_1 (
    .OP0(Opcode[0]), .OP1(Opcode[1]), .OP2(Opcode[2]), .OP3(Opcode[3]), .OP4(Opcode[4]), .F0(Function[0]),
    .F1(Function[1]), .RegWrite(RegWrite), .RegDest0(RegDest[0]), .RegDest1(RegDest[1]),
    .RegWSrc0(RegWSrc[0]), .RegWSrc1(RegWSrc[1]), .memoryRead(memoryRead), .memoryWrite(memoryWrite));
  ProgramCounterControlUnit programcountercontrolunit_1 (
    .OP2(Opcode[0]), .OP1(Opcode[1]), .OP0(Opcode[2]), .PCSrc1(PCSrc[0]), .BrachOP0(PCSrc[1]));  // open: OP4, OP3, PCSrc0, BranchOP1, JumpOP
endmodule

module ALUControlUnit (
  input  OP0,
  input  OP1,
  input  OP2,
  input  OP3,
  input  OP4,
  input  F0,
  input  F1,
  output ALUop0,
  output ALUop1,
  output ALUop2,
  output ALUop3,
  output ALUSrc,
  output signExtend
);
endmodule

module RegistersMemoryControlUnit (
  input  OP0,
  input  OP1,
  input  OP2,
  input  OP3,
  input  OP4,
  input  F0,
  input  F1,
  output RegWrite,
  output RegDest0,
  output RegDest1,
  output RegWSrc0,
  output RegWSrc1,
  output memoryRead,
  output memoryWrite
);
endmodule

module ProgramCounterControlUnit (
  input  OP4,
  input  OP3,
  input  OP2,
  input  OP1,
  input  OP0,
  output PCSrc0,
  output PCSrc1,
  output BrachOP0,
  output BranchOP1,
  output JumpOP
);

  wire and_1_out, and_2_out, and_3_out, and_4_out, and_5_out, and_6_out, and_7_out, not_1_out, not_2_out,
       not_3_out, not_4_out, not_5_out, not_6_out, not_7_out, not_8_out, not_11_out;

  not not_1 (not_1_out, OP4);
  not not_2 (not_2_out, OP2);
  not not_3 (not_3_out, OP3);
  not not_4 (not_4_out, OP4);
  not not_5 (not_5_out, OP3);
  not not_6 (not_6_out, OP4);
  not not_7 (not_7_out, OP1);
  not not_8 (not_8_out, OP2);
  not not_9 (BranchOP1, OP1);
  not not_10 (JumpOP, OP3);
  not not_11 (not_11_out, OP1);
  and and_1 (and_1_out, not_1_out, OP2);
  and and_2 (and_2_out, OP3, not_2_out);
  and and_3 (and_3_out, OP4, not_3_out);
  and and_4 (and_4_out, not_4_out, not_5_out);
  and and_5 (and_5_out, not_6_out, not_7_out);
  and and_6 (and_6_out, not_8_out, OP1);
  and and_7 (and_7_out, OP4, OP2);
  or or_1 (PCSrc0, not_11_out, and_1_out, and_2_out, and_3_out);
  or or_2 (PCSrc1, and_4_out, and_5_out, and_6_out, and_7_out);

  assign BrachOP0 = OP0;
endmodule
