// Logisim project JBControl.circ as structural Verilog
module JumpControl (
  input  [15:0] PC,
  input  [15:0] Rs,
  input  [10:0] Imm1,
  input  JOperation,
  output [15:0] newPC
);

  wire [15:0] adder_1_out, Imm;

  assign Imm = {{5{Imm1[10]}}, Imm1};  // Bit_Extender bit_extender_1
  Adder #(.width(16)) adder_1 (.a(PC), .b(Imm), .out(adder_1_out), .cin(1'b0));  // open: cout
  Multiplexer #(.width(16), .enable("false")) multiplexer_1 (
    .in0(adder_1_out), .in1(Rs), .out(newPC), .sel(JOperation));
endmodule

module BranchControl (
  input  [1:0] Operation,
  input  Zero,
  input  Less_Than,
  input  [4:0] Imm5,
  input  [15:0] PC,
  output [15:0] newPC
);

  wire not_1_out;
  wire [15:0] Beq, Imm16, updatedPC;

  assign Imm16 = {{11{Imm5[4]}}, Imm5};  // Bit_Extender bit_extender_1
  assign Beq = not_1_out ? PC : 16'bz;  // Controlled_Buffer controlled_buffer_1
  not not_1 (not_1_out, Zero);
  assign Beq = Zero ? updatedPC : 16'bz;  // Controlled_Buffer controlled_buffer_2

  // Other names for the same wires on the sheet: Less = Less_Than
endmodule
