// Logisim project PipelinedProcessor.circ as structural Verilog: 4 circuits, main circuit main
module main (
);

  wire ALUSrc, BranchTaken, Bubble, clk, DisableIR, DisablePC, Ex_ALUSrc, Ex_MemoryRead, Ex_RegWrite,
       Ex_signExtend, Flush, JumpOP, Mem_MemoryRead, Mem_MemoryWrite, Mem_RegWrite, MemoryRead, MemoryWrite,
       not_1_out, not_2_out, not_3_out, RegWrite, signExtend, WB_RegWrite;
  wire [0:0] and_2_out, Ex_MEMsignals, ID_PCSrc;
  wire [1:0] BranchOP, ExecutionSrc, F, ForwardA, ForwardB, MemorySrc, PCSrc, RegDest, RegisterWSrc,
       WB_RegDest, WB_RegisterWSrc, WriteBackSrc;
  wire [2:0] Ex_Rd, ID_Rd, Mem_Rd, Rd, Rs, Rt, WB_Rd;
  wire [3:0] ALUop, Ex_ALUop, Ex_WBsignals, Mem_WBsignals;
  wire [4:0] Ex_Imm5, Ex_Opcode, Imm5, Mem_Opcode, Opcode, WB_Opcode;
  wire [4:4] and_1_out;
  wire [10:0] Ex_Imm11, Imm11;
  wire [15:0] A, B, bit_extender_1_out, bit_extender_2_out, bit_extender_3_out, Ex_ALUout, Ex_ReturnAddress,
       Ex_Rs, Ex_Rt, Ex_ShiftedImm, extendedImmediate, ID_BranchPC, ID_JumpPC, ID_PC, ID_ReturnAdress, IR,
       Mem_ALUout, Mem_MemoryData, Mem_ReturnAddress, Mem_Rt, Mem_ShiftedImm, Mem_ShiftedImmediate,
       multiplexer_1_out, multiplexer_2_out, multiplexer_4_out, multiplexer_5_out, multiplexer_6_out,
       multiplexer_7_out, multiplexer_8_out, multiplexer_9_out, multiplexer_12_out, PC, PC_1, R1, R2, R3, R4,
       R5, R6, R7, RegisterWrite, rom_1_data, RsValue, RtValue, WB_ALUout, WB_MemoryData, WB_ReturnAddress,
       WB_ShiftedImm, WB_ShiftedImmediate;

  Multiplexer #(.select(2), .width(16), .enable("false")) multiplexer_1 (
    .in0(PC_1), .in1(ID_JumpPC), .in2(ID_BranchPC), .out(multiplexer_1_out), .sel({BranchTaken, ID_PCSrc[0]}));  // open: in3
  // Probe on {BranchTaken, ID_PCSrc[0]}
  not not_1 (not_1_out, DisablePC);
  // Probe on R1
  // Probe on R2
  // Probe on R3
  // Probe on R4
  // Probe on R5
  // Probe on R6
  // Probe on R7
  Register #(.width(16)) register_1 (.D(multiplexer_1_out), .en(not_1_out), .Q(PC), .clk(clk));  // open: clr
  Adder #(.width(16)) adder_1 (.a(16'h1), .b(PC), .out(PC_1), .cin(1'b0));  // open: cout
  ROM #(.addrWidth(16), .dataWidth(16)) rom_1 (.addr(PC), .data(rom_1_data), .sel(1'b1));
  Multiplexer #(.width(16), .enable("false")) multiplexer_2 (
    .in0(rom_1_data), .in1({16{1'b0}}), .out(multiplexer_2_out), .sel(Flush));
  Register #(.width(16)) PCRegister (.D(PC), .Q(ID_PC), .clk(clk));  // open: en, clr
  Register #(.width(16)) ReturnAddress (.D(PC_1), .Q(ID_ReturnAdress), .clk(clk));  // open: en, clr
  Register #(.width(16)) InstructionRegister (.D(multiplexer_2_out), .en(not_2_out), .Q(IR), .clk(clk));  // open: clr
  not not_2 (not_2_out, DisableIR);
  // Probe on Opcode
  InstructionSplitter instructionsplitter_1 (
    .Instruction(IR), .Op(Opcode), .F(F), .Rd(Rd), .Rs(Rs), .Rt(Rt), .Imm5(Imm5), .Imm11(Imm11));
  ControlUnit controlunit_1 (
    .Opcode(Opcode), .Function(F), .ALUop(ALUop), .ALUSrc(ALUSrc), .signExtend(signExtend),
    .RegWrite(RegWrite), .RegDest(RegDest), .RegWSrc(RegisterWSrc), .memoryRead(MemoryRead),
    .memoryWrite(MemoryWrite), .PCSrc(PCSrc), .BrachOP(BranchOP), .JumpOP(JumpOP));
  Clock clock_1 (.out(clk));
  // Probe on Rs
  // Probe on Rt
  // Probe on Rd
  // Probe on Imm5
  // Probe on Imm11
  // Probe on BranchOP
  // Probe on ID_Rd
  Multiplexer #(.select(2), .width(3), .enable("false")) multiplexer_3 (
    .in0(Rt), .in1(Rd), .in2(3'b001), .in3(3'b111), .out(ID_Rd), .sel(RegDest));
  JumpControl jumpcontrol_1 (
    .PC(ID_PC), .Rs(A), .Imm1(Imm11), .newPC(ID_JumpPC), .JOperation(JumpOP), .PCSrc(PCSrc),
    .JumpTaken(ID_PCSrc[0]));
  BranchControl branchcontrol_1 (
    .Operation(BranchOP), .Imm5(Imm5), .PC(ID_PC), .newPC(ID_BranchPC), .A(A), .B(B),
    .BranchTaken(BranchTaken), .PCSrc(PCSrc));
  or or_1 (Flush, BranchTaken, ID_PCSrc[0]);
  // RegisterFile registerfile_1: pin names not known; wires that end beside it: Rs, Rt, WB_Rd, RsValue
  Multiplexer #(.select(2), .width(16), .enable("false")) multiplexer_4 (
    .in0(WB_ALUout), .in1(WB_ShiftedImm), .in2(WB_ReturnAddress), .in3(WB_MemoryData),
    .out(multiplexer_4_out), .sel(WriteBackSrc));
  Multiplexer #(.select(2), .width(16), .enable("false")) multiplexer_5 (
    .in0(WB_ALUout), .in1(WB_ShiftedImm), .in2(WB_ReturnAddress), .in3(WB_MemoryData),
    .out(multiplexer_5_out), .sel(WriteBackSrc));
  ForwardingSourceControl forwardingsourcecontrol_1 (
    .OP4(Mem_Opcode[4]), .OP3(Mem_Opcode[3]), .OP2(Mem_Opcode[2]), .OP1(Mem_Opcode[1]), .OP0(Mem_Opcode[0]),
    .S1(MemorySrc[1]), .S0(MemorySrc[0]));
  // Probe on MemorySrc
  Multiplexer #(.select(2), .width(16), .enable("false")) multiplexer_6 (
    .in0(Mem_ALUout), .in1(Mem_ShiftedImm), .in2(Mem_ReturnAddress), .in3(Mem_MemoryData),
    .out(multiplexer_6_out), .sel(MemorySrc));
  Multiplexer #(.select(2), .width(16), .enable("false")) multiplexer_7 (
    .in0(Mem_ALUout), .in1(Mem_ShiftedImm), .in2(Mem_ReturnAddress), .in3(Mem_MemoryData),
    .out(multiplexer_7_out), .sel(MemorySrc));
  ForwardingControl forwardingcontrol_1 (
    .Rs(Rs), .Rd2(Ex_Rd), .Rd3(Mem_Rd), .Ex_RegWrite(Ex_RegWrite), .Mem_RegWrite(Mem_RegWrite),
    .Forwarding(ForwardA), .WB_RegWrite(WB_RegWrite), .Rd4(WB_Rd));
  ForwardingControl forwardingcontrol_2 (
    .Rs(Rt), .Rd2(Ex_Rd), .Rd3(Mem_Rd), .Ex_RegWrite(Ex_RegWrite), .Mem_RegWrite(Mem_RegWrite),
    .Forwarding(ForwardB), .WB_RegWrite(WB_RegWrite), .Rd4(WB_Rd));
  StallControl stallcontrol_1 (
    .Ex_MemRead(Ex_MemoryRead), .ForwardA(ForwardA), .ForwardB(ForwardB), .DisablePC(DisablePC),
    .DisableIR(DisableIR), .InsertBubble(Bubble));
  ForwardingSourceControl forwardingsourcecontrol_2 (
    .OP4(WB_Opcode[4]), .OP3(WB_Opcode[3]), .OP2(WB_Opcode[2]), .OP1(WB_Opcode[1]), .OP0(WB_Opcode[0]),
    .S1(WriteBackSrc[1]), .S0(WriteBackSrc[0]));
  // Probe on ForwardA
  // Probe on ForwardB
  ForwardingSourceControl forwardingsourcecontrol_3 (
    .OP4(Ex_Opcode[4]), .OP3(Ex_Opcode[3]), .OP2(Ex_Opcode[2]), .OP1(Ex_Opcode[1]), .OP0(Ex_Opcode[0]),
    .S1(ExecutionSrc[1]), .S0(ExecutionSrc[0]));
  Multiplexer #(.select(2), .width(16), .enable("false")) multiplexer_8 (
    .in0(Ex_ALUout), .in1(Ex_ShiftedImm), .in2(Ex_ReturnAddress), .out(multiplexer_8_out), .sel(ExecutionSrc));  // open: in3
  Multiplexer #(.select(2), .width(16), .enable("false")) multiplexer_9 (
    .in0(Ex_ALUout), .in1(Ex_ShiftedImm), .in2(Ex_ReturnAddress), .out(multiplexer_9_out), .sel(ExecutionSrc));  // open: in3
  // Probe on ExecutionSrc
  and and_1 (and_1_out[4], RegWrite, Bubble);
  and and_2 (and_2_out[0], MemoryWrite, Bubble);
  Multiplexer #(.select(2), .width(16), .enable("false")) multiplexer_10 (
    .in0(RsValue), .in1(multiplexer_8_out), .in2(multiplexer_6_out), .in3(multiplexer_4_out), .out(A),
    .sel(ForwardA));
  Multiplexer #(.select(2), .width(16), .enable("false")) multiplexer_11 (
    .in0(RtValue), .in1(multiplexer_9_out), .in2(multiplexer_7_out), .in3(multiplexer_5_out), .out(B),
    .sel(ForwardB));
  Register #(.width(16)) ReturnAddressRegister (.D(ID_ReturnAdress), .Q(Ex_ReturnAddress), .clk(clk));  // open: en, clr
  Register #(.width(11)) u_imm11 (.D(Imm11), .Q(Ex_Imm11), .clk(clk));  // open: en, clr
  Register #(.width(5)) u_imm5 (.D(Imm5), .Q(Ex_Imm5), .clk(clk));  // open: en, clr
  Register #(.width(16)) OperandA (.D(A), .Q(Ex_Rs), .clk(clk));  // open: en, clr
  Register #(.width(16)) OperandB (.D(B), .Q(Ex_Rt), .clk(clk));  // open: en, clr
  Register #(.width(3)) Rd2 (.D(ID_Rd), .Q(Ex_Rd), .clk(clk));  // open: en, clr
  Register #(.width(6)) ExecutionSignals (
    .D({signExtend, ALUSrc, ALUop}), .Q({Ex_signExtend, Ex_ALUSrc, Ex_ALUop}), .clk(clk));  // open: en, clr
  Register #(.width(5)) WriteBackSignals (
    .D({and_1_out[4], RegDest, RegisterWSrc}), .Q({Ex_RegWrite, Ex_WBsignals}), .clk(clk));  // open: en, clr
  Register #(.width(2)) MemorySignals (
    .D({MemoryRead, and_2_out[0]}), .Q({Ex_MemoryRead, Ex_MEMsignals[0]}), .clk(clk));  // open: en, clr
  Register #(.width(5)) u_Opcode (.D(Opcode), .Q(Ex_Opcode), .clk(clk));  // open: en, clr
  // Probe on Ex_Imm11
  Multiplexer #(.width(16), .enable("false")) multiplexer_12 (
    .in0(Ex_Rt), .in1(extendedImmediate), .out(multiplexer_12_out), .sel(Ex_ALUSrc));
  assign bit_extender_1_out = {{11{1'b0}}, Ex_Imm5};  // Bit_Extender bit_extender_1
  not not_3 (not_3_out, Ex_signExtend);
  assign bit_extender_2_out = {{11{Ex_Imm5[4]}}, Ex_Imm5};  // Bit_Extender bit_extender_2
  assign extendedImmediate = not_3_out ? bit_extender_1_out : 16'bz;  // Controlled_Buffer controlled_buffer_1
  assign extendedImmediate = Ex_signExtend ? bit_extender_2_out : 16'bz;  // Controlled_Buffer controlled_buffer_2
  assign bit_extender_3_out = {{5{1'b0}}, Ex_Imm11};  // Bit_Extender bit_extender_3
  Shifter #(.width(16)) shifter_1 (.in(bit_extender_3_out), .\dist (4'b0101), .out(Ex_ShiftedImm));
  // Probe on Ex_ShiftedImm
  ALU alu_1 (.in_1(Ex_ALUop), .in_2(Ex_Rs), .in_3(multiplexer_12_out), .out_6(Ex_ALUout));  // open: out_4, out_5
  Register #(.width(16)) ReturnAddressRegister_2 (
    .D(Ex_ReturnAddress), .Q(Mem_ReturnAddress), .clk(clk));  // open: en, clr
  Register #(.width(16)) RtValueRegister (.D(Ex_Rt), .Q(Mem_Rt), .clk(clk));  // open: en, clr
  Register #(.width(3)) Rd3 (.D(Ex_Rd), .Q(Mem_Rd), .clk(clk));  // open: en, clr
  Register #(.width(5)) WriteBackSignals_2 (
    .D({Ex_RegWrite, Ex_WBsignals}), .Q({Mem_RegWrite, Mem_WBsignals}), .clk(clk));  // open: en, clr
  Register #(.width(2)) MemorySignals_2 (
    .D({Ex_MemoryRead, Ex_MEMsignals[0]}), .Q({Mem_MemoryRead, Mem_MemoryWrite}), .clk(clk));  // open: en, clr
  Register #(.width(16)) ALU_Output (.D(Ex_ALUout), .Q(Mem_ALUout), .clk(clk));  // open: en, clr
  Register #(.width(16)) Shifted_Immediate (.D(Ex_ShiftedImm), .Q(Mem_ShiftedImmediate), .clk(clk));  // open: en, clr
  Register #(.width(5)) Opcode_2 (.D(Ex_Opcode), .Q(Mem_Opcode), .clk(clk));  // open: en, clr
  // Probe on Mem_ShiftedImmediate
  Data_Memory data_memory_1 (
    .CLK(clk), .Memory_Enable(1'b1), .Memory_Read(Mem_MemoryRead), .Memory_Write(Mem_MemoryWrite),
    .Address(Mem_ALUout), .Data_In(Mem_Rt), .Data_Out(Mem_MemoryData));
  Register #(.width(16)) ReturnAddressRegister_3 (
    .D(Mem_ReturnAddress), .Q(WB_ReturnAddress), .clk(clk));  // open: en, clr
  Register #(.width(3)) Rd3_2 (.D(Mem_Rd), .Q(WB_Rd), .clk(clk));  // open: en, clr
  Register #(.width(5)) WriteBackSignals_3 (
    .D({Mem_RegWrite, Mem_WBsignals}), .Q({WB_RegWrite, WB_RegDest, WB_RegisterWSrc}), .clk(clk));  // open: en, clr
  Register #(.width(16)) ALU_Output_2 (.D(Mem_ALUout), .Q(WB_ALUout), .clk(clk));  // open: en, clr
  Register #(.width(16)) Shifted_Immediate_2 (
    .D(Mem_ShiftedImmediate), .Q(WB_ShiftedImmediate), .clk(clk));  // open: en, clr
  Register #(.width(16)) Memory (.D(Mem_MemoryData), .Q(WB_MemoryData), .clk(clk));  // open: en, clr
  Register #(.width(5)) Opcode_3 (.D(Mem_Opcode), .Q(WB_Opcode), .clk(clk));  // open: en, clr
  // Probe on WB_ShiftedImmediate
  // Probe on WB_MemoryData
  Multiplexer #(.select(2), .width(16), .enable("false")) multiplexer_13 (
    .in0(WB_ALUout), .in1(WB_MemoryData), .in2(WB_ShiftedImmediate), .in3(WB_ReturnAddress),
    .out(RegisterWrite), .sel(WB_RegisterWSrc));

  // Other names for the same wires on the sheet: Ex_MEMsignals[1] = Ex_MemoryRead; Ex_WBsignals[4] = Ex_RegWrite;
  //   JumpTaken = ID_PCSrc[0]; ID_PCSrc[1] = BranchTaken; Mem_WBsignals[4] = Mem_RegWrite

  // Notes on the sheet:
  //   Instruction Fetch
  //   contents of rom_1 (hex, n*v repeats v):
  //   3a09 3892 385b 7119 385b 4052 f7fd f000
  //   Instruction Decode
  //   Execution
  //   Memory
  //   Write Back
endmodule

module ForwardingSourceControl (
  input  OP4,
  input  OP3,
  input  OP2,
  input  OP1,
  input  OP0,
  output S1,
  output S0
);

  wire and_2_out, and_3_out, not_1_out, not_2_out;

  and and_1 (S1, OP3, OP2);
  not not_1 (not_1_out, OP1);
  not not_2 (not_2_out, OP3);
  and and_2 (and_2_out, OP3, OP2, not_1_out);
  and and_3 (and_3_out, OP4, not_2_out);
  or or_1 (S0, and_2_out, and_3_out);
endmodule

module ForwardingControl (
  input  [2:0] Rs,
  input  [2:0] Rd2,
  input  [2:0] Rd3,
  input  [2:0] Rd4,
  input  Ex_RegWrite,
  input  Mem_RegWrite,
  input  WB_RegWrite,
  output [1:0] Forwarding
);

  wire and_4_out, and_5_out, comparator_1_eq, Forward0, Forward1, Forward2, Forward3, not_3_out, not_4_out,
       not_5_out, or_1_out, Rs__0, Rs__Rd2, Rs__Rd3, Rs__Rd4;

  Comparator #(.width(3)) comparator_1 (.a(Rs), .b(3'b000), .eq(comparator_1_eq));  // open: gt, lt
  not not_1 (Rs__0, comparator_1_eq);
  Comparator #(.width(3), .mode("unsigned")) comparator_2 (.a(Rs), .b(Rd2), .eq(Rs__Rd2));  // open: gt, lt
  Comparator #(.width(3), .mode("unsigned")) comparator_3 (.a(Rs), .b(Rd3), .eq(Rs__Rd3));  // open: gt, lt
  Comparator #(.width(3), .mode("unsigned")) comparator_4 (.a(Rs), .b(Rd4), .eq(Rs__Rd4));  // open: gt, lt
  and and_1 (Forward1, Rs__0, Rs__Rd2, Ex_RegWrite);
  and and_2 (Forward2, Rs__0, Rs__Rd3, Mem_RegWrite);
  and and_3 (Forward3, Rs__0, Rs__Rd4, WB_RegWrite);
  or or_1 (or_1_out, Forward1, Forward2, Forward3);
  not not_2 (Forward0, or_1_out);
  and and_4 (and_4_out, not_3_out, Forward2);
  not not_3 (not_3_out, Forward1);
  and and_5 (and_5_out, not_4_out, Forward3, not_5_out);
  not not_4 (not_4_out, Forward1);
  assign Forwarding = Forward1 ? 2'b01 : 2'bz;  // Controlled_Buffer controlled_buffer_1
  assign Forwarding = and_4_out ? 2'b10 : 2'bz;  // Controlled_Buffer controlled_buffer_2
  assign Forwarding = and_5_out ? 2'b11 : 2'bz;  // Controlled_Buffer controlled_buffer_3
  not not_5 (not_5_out, Forward2);
  assign Forwarding = Forward0 ? 2'b00 : 2'bz;  // Controlled_Buffer controlled_buffer_4

  // Other names for the same wires on the sheet: ForwardingSelection[1:0] = Forwarding
endmodule

module StallControl (
  input  Ex_MemRead,
  input  [1:0] ForwardA,
  input  [1:0] ForwardB,
  output DisablePC,
  output DisableIR,
  output InsertBubble
);

  wire ForwardA__1, ForwardB__1, or_1_out;

  Comparator #(.width(2)) comparator_1 (.a(ForwardA), .b(2'b01), .eq(ForwardA__1));  // open: gt, lt
  Comparator #(.width(2)) comparator_2 (.a(ForwardB), .b(2'b01), .eq(ForwardB__1));  // open: gt, lt
  not not_1 (InsertBubble, DisableIR);
  or or_1 (or_1_out, ForwardA__1, ForwardB__1);
  and and_1 (DisableIR, or_1_out, Ex_MemRead);

  assign DisablePC = DisableIR;

  // Other names for the same wires on the sheet: Stall = DisableIR
endmodule
