// Logisim project RegisterFileC.circ as structural Verilog: 1 circuit, main circuit RegisterFile
module RegisterFile (
  input  Reg_Write,
  input  CLK,
  input  [4:0] RA,
  input  [4:0] RB,
  input  [4:0] RW,
  input  [31:0] Bus_W,
  output [31:0] Bus_A,
  output [31:0] Bus_B
);

  wire S1, S2, S3, S4, S5, S6, S7, S8, S9, S10, S11, S12, S13, S14, S15, S16, S17, S18, S19, S20, S21, S22,
       S23, S24, S25, S26, S27, S28, S29, S30, S31;
  wire [31:0] R1, R2, R3, R4, R5, R6, R7, R8, R9, R10, R11, R12, R13, R14, R15, R16, R17, R18, R19, R20, R21,
       R22, R23, R24, R25, R26, R27, R28, R29, R30, R31;

  FRU fru_1 (.RegEn(S1), .CLK(CLK), .RegWrite(Reg_Write), .BusW(Bus_W), .BusR(R1));
  FRU fru_2 (.RegEn(S6), .CLK(CLK), .RegWrite(Reg_Write), .BusW(Bus_W), .BusR(R6));
  FRU fru_3 (.RegEn(S11), .CLK(CLK), .RegWrite(Reg_Write), .BusW(Bus_W), .BusR(R11));
  FRU fru_4 (.RegEn(S16), .CLK(CLK), .RegWrite(Reg_Write), .BusW(Bus_W), .BusR(R16));
  FRU fru_5 (.RegEn(S21), .CLK(CLK), .RegWrite(Reg_Write), .BusW(Bus_W), .BusR(R21));
  FRU fru_6 (.RegEn(S26), .CLK(CLK), .RegWrite(Reg_Write), .BusW(Bus_W), .BusR(R26));
  Decoder #(.select(5), .enable("false")) decoder_1 (
    .out1(S1), .out2(S2), .out3(S3), .out4(S4), .out5(S5), .out6(S6), .out7(S7), .out8(S8), .out9(S9),
    .out10(S10), .out11(S11), .out12(S12), .out13(S13), .out14(S14), .out15(S15), .out16(S16), .out17(S17),
    .out18(S18), .out19(S19), .out20(S20), .out21(S21), .out22(S22), .out23(S23), .out24(S24), .out25(S25),
    .out26(S26), .out27(S27), .out28(S28), .out29(S29), .out30(S30), .out31(S31), .sel(RW));  // open: out0
  FRU fru_7 (.RegEn(S2), .CLK(CLK), .RegWrite(Reg_Write), .BusW(Bus_W), .BusR(R2));
  FRU fru_8 (.RegEn(S7), .CLK(CLK), .RegWrite(Reg_Write), .BusW(Bus_W), .BusR(R7));
  FRU fru_9 (.RegEn(S12), .CLK(CLK), .RegWrite(Reg_Write), .BusW(Bus_W), .BusR(R12));
  FRU fru_10 (.RegEn(S17), .CLK(CLK), .RegWrite(Reg_Write), .BusW(Bus_W), .BusR(R17));
  FRU fru_11 (.RegEn(S22), .CLK(CLK), .RegWrite(Reg_Write), .BusW(Bus_W), .BusR(R22));
  FRU fru_12 (.RegEn(S27), .CLK(CLK), .RegWrite(Reg_Write), .BusW(Bus_W), .BusR(R27));
  FRU fru_13 (.RegEn(S3), .CLK(CLK), .RegWrite(Reg_Write), .BusW(Bus_W), .BusR(R3));
  FRU fru_14 (.RegEn(S8), .CLK(CLK), .RegWrite(Reg_Write), .BusW(Bus_W), .BusR(R8));
  FRU fru_15 (.RegEn(S13), .CLK(CLK), .RegWrite(Reg_Write), .BusW(Bus_W), .BusR(R13));
  FRU fru_16 (.RegEn(S18), .CLK(CLK), .RegWrite(Reg_Write), .BusW(Bus_W), .BusR(R18));
  FRU fru_17 (.RegEn(S23), .CLK(CLK), .RegWrite(Reg_Write), .BusW(Bus_W), .BusR(R23));
  FRU fru_18 (.RegEn(S28), .CLK(CLK), .RegWrite(Reg_Write), .BusW(Bus_W), .BusR(R28));
  FRU fru_19 (.RegEn(S31), .CLK(CLK), .RegWrite(Reg_Write), .BusW(Bus_W), .BusR(R31));
  RegisterSelector registerselector_1 (
    .R1(R1), .R5(R5), .R9(R9), .R13(R13), .R17(R17), .R21(R21), .R25(R25), .R29(R29), .Register_S(RA),
    .R2(R2), .R6(R6), .R10(R10), .R14(R14), .R18(R18), .R22(R22), .R26(R26), .R30(R30), .R3(R3), .R7(R7),
    .R11(R11), .R15(R15), .R19(R19), .R23(R23), .R27(R27), .R31(R31), .R4(R4), .R8(R8), .R12(R12), .R16(R16),
    .R20(R20), .R24(R24), .R28(R28), .out_33(Bus_A));
  FRU fru_20 (.RegEn(S4), .CLK(CLK), .RegWrite(Reg_Write), .BusW(Bus_W), .BusR(R4));
  FRU fru_21 (.RegEn(S9), .CLK(CLK), .RegWrite(Reg_Write), .BusW(Bus_W), .BusR(R9));
  FRU fru_22 (.RegEn(S14), .CLK(CLK), .RegWrite(Reg_Write), .BusW(Bus_W), .BusR(R14));
  FRU fru_23 (.RegEn(S19), .CLK(CLK), .RegWrite(Reg_Write), .BusW(Bus_W), .BusR(R19));
  FRU fru_24 (.RegEn(S24), .CLK(CLK), .RegWrite(Reg_Write), .BusW(Bus_W), .BusR(R24));
  FRU fru_25 (.RegEn(S29), .CLK(CLK), .RegWrite(Reg_Write), .BusW(Bus_W), .BusR(R29));
  FRU fru_26 (.RegEn(S5), .CLK(CLK), .RegWrite(Reg_Write), .BusW(Bus_W), .BusR(R5));
  FRU fru_27 (.RegEn(S10), .CLK(CLK), .RegWrite(Reg_Write), .BusW(Bus_W), .BusR(R10));
  FRU fru_28 (.RegEn(S15), .CLK(CLK), .RegWrite(Reg_Write), .BusW(Bus_W), .BusR(R15));
  FRU fru_29 (.RegEn(S20), .CLK(CLK), .RegWrite(Reg_Write), .BusW(Bus_W), .BusR(R20));
  FRU fru_30 (.RegEn(S25), .CLK(CLK), .RegWrite(Reg_Write), .BusW(Bus_W), .BusR(R25));
  FRU fru_31 (.RegEn(S30), .CLK(CLK), .RegWrite(Reg_Write), .BusW(Bus_W), .BusR(R30));
  RegisterSelector registerselector_2 (
    .R1(R1), .R5(R5), .R9(R9), .R13(R13), .R17(R17), .R21(R21), .R25(R25), .R29(R29), .Register_S(RB),
    .R2(R2), .R6(R6), .R10(R10), .R14(R14), .R18(R18), .R22(R22), .R26(R26), .R30(R30), .R3(R3), .R7(R7),
    .R11(R11), .R15(R15), .R19(R19), .R23(R23), .R27(R27), .R31(R31), .R4(R4), .R8(R8), .R12(R12), .R16(R16),
    .R20(R20), .R24(R24), .R28(R28), .out_33(Bus_B));
endmodule
