// Logisim project ShiftLeftLogically.circ as structural Verilog: 1 circuit, main circuit SLL
module SLL (
  input  [15:0] Operand,
  input  [3:0] Shift_Amount
);

  wire S0, S1, S2, S3, S4, S5, S6, S7, S8, S9;

  Multiplexer #(.select(4), .enable("false")) multiplexer_1 (
    .in0(Operand[0]), .in1(1'b0), .in2(1'b0), .in3(1'b0), .in4(1'b0), .in5(1'b0), .in6(1'b0), .in7(1'b0),
    .in8(1'b0), .in9(1'b0), .in10(1'b0), .in11(1'b0), .in12(1'b0), .in13(1'b0), .in14(1'b0), .in15(1'b0),
    .out(S0), .sel(Shift_Amount));
  Multiplexer #(.select(4), .enable("false")) multiplexer_2 (
    .in0(Operand[1]), .in1(Operand[0]), .in2(1'b0), .in3(1'b0), .in4(1'b0), .in5(1'b0), .in6(1'b0),
    .in7(1'b0), .in8(1'b0), .in9(1'b0), .in10(1'b0), .in11(1'b0), .in12(1'b0), .in13(1'b0), .in14(1'b0),
    .in15(1'b0), .out(S1), .sel(Shift_Amount));
  Multiplexer #(.select(4), .enable("false")) multiplexer_3 (
    .in0(Operand[2]), .in1(Operand[1]), .in2(Operand[0]), .in3(1'b0), .in4(1'b0), .in5(1'b0), .in6(1'b0),
    .in7(1'b0), .in8(1'b0), .in9(1'b0), .in10(1'b0), .in11(1'b0), .in12(1'b0), .in13(1'b0), .in14(1'b0),
    .in15(1'b0), .out(S2), .sel(Shift_Amount));
  Multiplexer #(.select(4), .enable("false")) multiplexer_4 (
    .in0(Operand[3]), .in1(Operand[2]), .in2(Operand[1]), .in3(Operand[0]), .in4(1'b0), .in5(1'b0),
    .in6(1'b0), .in7(1'b0), .in8(1'b0), .in9(1'b0), .in10(1'b0), .in11(1'b0), .in12(1'b0), .in13(1'b0),
    .in14(1'b0), .in15(1'b0), .out(S3), .sel(Shift_Amount));
  Multiplexer #(.select(4), .enable("false")) multiplexer_5 (
    .in0(Operand[4]), .in1(Operand[3]), .in2(Operand[2]), .in3(Operand[1]), .in4(Operand[0]), .in5(1'b0),
    .in6(1'b0), .in7(1'b0), .in8(1'b0), .in9(1'b0), .in10(1'b0), .in11(1'b0), .in12(1'b0), .in13(1'b0),
    .in14(1'b0), .in15(1'b0), .out(S4), .sel(Shift_Amount));
  Multiplexer #(.select(4), .enable("false")) multiplexer_6 (
    .in0(Operand[5]), .in1(Operand[4]), .in2(Operand[3]), .in3(Operand[2]), .in4(Operand[1]),
    .in5(Operand[0]), .in6(1'b0), .in7(1'b0), .in8(1'b0), .in9(1'b0), .in10(1'b0), .in11(1'b0), .in12(1'b0),
    .in13(1'b0), .in14(1'b0), .in15(1'b0), .out(S5), .sel(Shift_Amount));
  Multiplexer #(.select(4), .enable("false")) multiplexer_7 (
    .in0(Operand[6]), .in1(Operand[5]), .in2(Operand[4]), .in3(Operand[3]), .in4(Operand[2]),
    .in5(Operand[1]), .in6(Operand[0]), .in7(1'b0), .in8(1'b0), .in9(1'b0), .in10(1'b0), .in11(1'b0),
    .in12(1'b0), .in13(1'b0), .in14(1'b0), .in15(1'b0), .out(S6), .sel(Shift_Amount));
  Multiplexer #(.select(4), .enable("false")) multiplexer_8 (
    .in0(Operand[7]), .in1(Operand[6]), .in2(Operand[5]), .in3(Operand[4]), .in4(Operand[3]),
    .in5(Operand[2]), .in6(Operand[1]), .in7(Operand[0]), .in8(1'b0), .in9(1'b0), .in10(1'b0), .in11(1'b0),
    .in12(1'b0), .in13(1'b0), .in14(1'b0), .in15(1'b0), .out(S7), .sel(Shift_Amount));
  Multiplexer #(.select(4), .enable("false")) multiplexer_9 (
    .in0(Operand[8]), .in1(Operand[7]), .in2(Operand[6]), .in3(Operand[5]), .in4(Operand[4]),
    .in5(Operand[3]), .in6(Operand[2]), .in7(Operand[1]), .in8(Operand[0]), .in9(1'b0), .in10(1'b0),
    .in11(1'b0), .in12(1'b0), .in13(1'b0), .in14(1'b0), .in15(1'b0), .out(S8), .sel(Shift_Amount));
  Multiplexer #(.select(4), .enable("false")) multiplexer_10 (
    .in0(Operand[9]), .in1(Operand[8]), .in2(Operand[7]), .in3(Operand[6]), .in4(Operand[5]),
    .in5(Operand[4]), .in6(Operand[3]), .in7(Operand[2]), .in8(Operand[1]), .in9(Operand[0]), .in10(1'b0),
    .in11(1'b0), .in12(1'b0), .in13(1'b0), .in14(1'b0), .in15(1'b0), .out(S9), .sel(Shift_Amount));

  // Other names for the same wires on the sheet: B0 = Operand[0]; B1 = Operand[1]; B2 = Operand[2]; B3 = Operand[3];
  //   B4 = Operand[4]; B5 = Operand[5]; B6 = Operand[6]; B7 = Operand[7]; B8 = Operand[8]; B9 = Operand[9];
  //   B10 = Operand[10]; B11 = Operand[11]; B12 = Operand[12]; B13 = Operand[13]; B14 = Operand[14];
  //   B15 = Operand[15]; SA[3:0] = Shift_Amount
endmodule
