// Logisim project file.circ as structural Verilog: 2 circuits, main circuit alu arithmetic
module alu_arithmetic (
  input  in_1,
  input  in_2,
  input  in_3,
  input  in_4,
  input  [15:0] in_5,
  input  in_6,
  input  in_7,
  input  [15:0] in_8,
  output out_9,
  output out_10,
  output out_11,
  output out_12,
  output out_13,
  output out_14,
  output out_15,
  output out_16,
  output out_17,
  output out_18,
  output out_19,
  output out_20,
  output out_21,
  output out_22,
  output out_23,
  output out_24,
  output out_25
);

  wire add_sub_1_out_7, add_sub_2_out_7, add_sub_3_out_7, add_sub_4_out_7, add_sub_5_out_7, add_sub_6_out_7,
       add_sub_7_out_7, add_sub_8_out_7, add_sub_9_out_7, add_sub_10_out_7, add_sub_11_out_7,
       add_sub_12_out_7, add_sub_13_out_7, add_sub_14_out_7, b0, b1, b2, b3, b4, b5, b6, b7, b8, b9, b10,
       b11, b12, b13, b14, b15, less, overflow, s0, s1, s2, s3, s4, s5, s6, s7, s8, s9, s10, s11, s12, s13,
       s14, s15;
  wire [15:0] bit_extender_1_out;

  Bit_Extender #(.in_width(5), .\type ("sign")) bit_extender_1 (.out(bit_extender_1_out));  // open: in
  Multiplexer #(.width(16), .enable("false")) multiplexer_1 (
    .in0(in_5), .in1(bit_extender_1_out),
    .out({b15, b14, b13, b12, b11, b10, b9, b8, b7, b6, b5, b4, b3, b2, b1, b0}), .sel(in_6));
  xor xor_1 (overflow, in_1, out_25);
  xor xor_2 (less, in_7, in_7);
  add_sub add_sub_1 (
    .in_1(in_1), .in_2(in_8[0]), .in_4(b0), .out_6(s0), .in_5(in_3), .in_3(in_2), .out_7(add_sub_1_out_7));
  add_sub add_sub_2 (
    .in_1(add_sub_1_out_7), .in_2(in_8[1]), .in_4(b1), .out_6(s1), .in_5(in_3), .in_3(in_2),
    .out_7(add_sub_2_out_7));
  add_sub add_sub_3 (
    .in_1(add_sub_2_out_7), .in_2(in_8[2]), .in_4(b2), .out_6(s2), .in_5(in_3), .in_3(in_2),
    .out_7(add_sub_3_out_7));
  add_sub add_sub_4 (
    .in_1(add_sub_3_out_7), .in_2(in_8[3]), .in_4(b3), .out_6(s3), .in_5(in_3), .in_3(in_2),
    .out_7(add_sub_4_out_7));
  add_sub add_sub_5 (
    .in_1(add_sub_4_out_7), .in_2(in_8[4]), .in_4(b4), .out_6(s4), .in_5(in_3), .in_3(in_2),
    .out_7(add_sub_5_out_7));
  add_sub add_sub_6 (
    .in_1(add_sub_5_out_7), .in_2(in_8[5]), .in_4(b5), .out_6(s5), .in_5(in_3), .in_3(in_2),
    .out_7(add_sub_6_out_7));
  add_sub add_sub_7 (
    .in_1(add_sub_6_out_7), .in_2(in_8[6]), .in_4(b6), .out_6(s6), .in_5(in_3), .in_3(in_2),
    .out_7(add_sub_7_out_7));
  add_sub add_sub_8 (
    .in_1(add_sub_7_out_7), .in_2(in_8[7]), .in_4(b7), .out_6(s7), .in_5(in_3), .in_3(in_2),
    .out_7(add_sub_8_out_7));
  add_sub add_sub_9 (
    .in_1(add_sub_8_out_7), .in_2(in_8[8]), .in_4(b8), .out_6(s8), .in_5(in_3), .in_3(in_2),
    .out_7(add_sub_9_out_7));
  add_sub add_sub_10 (
    .in_1(add_sub_9_out_7), .in_2(in_8[9]), .in_4(b9), .out_6(s9), .in_5(in_3), .in_3(in_2),
    .out_7(add_sub_10_out_7));
  add_sub add_sub_11 (
    .in_1(add_sub_10_out_7), .in_2(in_8[10]), .in_4(b10), .out_6(s10), .in_5(in_3), .in_3(in_2),
    .out_7(add_sub_11_out_7));
  add_sub add_sub_12 (
    .in_1(add_sub_11_out_7), .in_2(in_8[11]), .in_4(b11), .out_6(s11), .in_5(in_3), .in_3(in_2),
    .out_7(add_sub_12_out_7));
  add_sub add_sub_13 (
    .in_1(add_sub_12_out_7), .in_2(in_8[12]), .in_4(b12), .out_6(s12), .in_5(in_3), .in_3(in_2),
    .out_7(add_sub_13_out_7));
  add_sub add_sub_14 (
    .in_1(add_sub_13_out_7), .in_2(in_8[13]), .in_4(b13), .out_6(s13), .in_5(in_3), .in_3(in_2),
    .out_7(add_sub_14_out_7));
  add_sub add_sub_15 (
    .in_1(add_sub_14_out_7), .in_2(in_8[14]), .in_4(b14), .out_6(s14), .in_5(in_3), .in_3(in_2), .out_7(in_1));
  add_sub add_sub_16 (.in_1(in_1), .in_2(in_8[15]), .in_4(b15), .out_6(s15), .in_5(in_3), .in_3(in_2), .out_7(out_25));
  Multiplexer #(.enable("false")) multiplexer_2 (.in0(s0), .in1(s15), .out(out_9), .sel(in_4));
  Multiplexer #(.enable("false")) multiplexer_3 (.in0(s1), .in1(less), .out(out_10), .sel(in_4));
  Multiplexer #(.enable("false")) multiplexer_4 (.in0(s12), .in1(less), .out(out_21), .sel(in_4));
  Multiplexer #(.enable("false")) multiplexer_5 (.in0(s13), .in1(less), .out(out_22), .sel(in_4));
  Multiplexer #(.enable("false")) multiplexer_6 (.in0(s14), .in1(less), .out(out_23), .sel(in_4));
  Multiplexer #(.enable("false")) multiplexer_7 (.in0(s2), .in1(less), .out(out_11), .sel(in_4));
  Multiplexer #(.enable("false")) multiplexer_8 (.in0(s3), .in1(less), .out(out_12), .sel(in_4));
  Multiplexer #(.enable("false")) multiplexer_9 (.in0(s4), .in1(less), .out(out_13), .sel(in_4));
  Multiplexer #(.enable("false")) multiplexer_10 (.in0(s5), .in1(less), .out(out_14), .sel(in_4));
  Multiplexer #(.enable("false")) multiplexer_11 (.in0(s6), .in1(less), .out(out_15), .sel(in_4));
  Multiplexer #(.enable("false")) multiplexer_12 (.in0(s7), .in1(less), .out(out_16), .sel(in_4));
  Multiplexer #(.enable("false")) multiplexer_13 (.in0(s8), .in1(less), .out(out_17), .sel(in_4));
  Multiplexer #(.enable("false")) multiplexer_14 (.in0(s9), .in1(less), .out(out_18), .sel(in_4));
  Multiplexer #(.enable("false")) multiplexer_15 (.in0(s10), .in1(less), .out(out_19), .sel(in_4));
  Multiplexer #(.enable("false")) multiplexer_16 (.in0(s11), .in1(less), .out(out_20), .sel(in_4));
  Multiplexer #(.enable("false")) multiplexer_17 (.in0(s15), .in1(less), .out(out_24), .sel(in_4));

  // Other names for the same wires on the sheet: ain = in_2; bin = in_3; cin = in_1; cout = out_25; a0 = in_8[0];
  //   a1 = in_8[1]; a2 = in_8[2]; a3 = in_8[3]; a4 = in_8[4]; a5 = in_8[5]; a6 = in_8[6]; a7 = in_8[7]; a8 = in_8[8];
  //   a9 = in_8[9]; a10 = in_8[10]; a11 = in_8[11]; a12 = in_8[12]; a13 = in_8[13]; a14 = in_8[14]; a15 = in_8[15];
  //   set = s15; signal = in_4

  // Notes on the sheet:
  //   B
  //   A
endmodule

module add_sub (
  input  in_1,
  input  in_2,
  input  in_3,
  input  in_4,
  input  in_5,
  output out_6,
  output out_7
);

  wire Ain, Bin, multiplexer_1_out, multiplexer_2_out;

  not not_1 (Ain, in_2);
  not not_2 (Bin, in_4);
  Multiplexer #(.enable("false")) multiplexer_1 (.in0(in_2), .in1(Ain), .out(multiplexer_1_out), .sel(in_3));
  Multiplexer #(.enable("false")) multiplexer_2 (.in0(in_4), .in1(Bin), .out(multiplexer_2_out), .sel(in_5));
  Adder #(.width(1)) adder_1 (.a(multiplexer_1_out), .b(multiplexer_2_out), .out(out_6), .cin(in_1), .cout(out_7));

  // Other names for the same wires on the sheet: A = in_2; B = in_4; cin = in_1
endmodule
